# Fritzing sketch simon (saved by Fritzing 0.7.10b)
breadboards: 1

parts:
  Arduino1 = Arduino
  R1 = Resistor [tolerance=±5% resistance=100 package=THT]
  R2 = Resistor [tolerance=±5% resistance=100 package=THT]
  R3 = Resistor [tolerance=±5% resistance=100 package=THT]
  R4 = Resistor [tolerance=±5% resistance=100 package=THT]
  R5 = Resistor [tolerance=±5% resistance=10k package=THT]
  R6 = Resistor [tolerance=±5% resistance=10k package=THT]
  R7 = Resistor [tolerance=±5% resistance=10k package=THT]
  R8 = Resistor [tolerance=±5% resistance=10k package=THT]
  LED1 = LED - 5mm [color="Red (633nm)" package="5 mm [THT]"]
  LED2 = LED - 5mm [color="Yellow (595nm)" package="5 mm [THT]"]
  LED3 = LED - 5mm [color="Green (565nm)" package="5 mm [THT]"]
  LED4 = LED - 5mm [color="Blue (525nm)" package="5 mm [THT]"]
  S1 = Pushbutton [package="[THT]"]
  S2 = Pushbutton [package="[THT]"]
  S3 = Pushbutton [package="[THT]"]
  S4 = Pushbutton [package="[THT]"]
  J1 = Piezo Speaker

nets:
  N1: Arduino1.D12, J1.pin2
  N2: Arduino1.D11, R8.Pin_0, S4.Pin_1, S4.Pin_2
  N3: Arduino1.D10, R7.Pin_0, S3.Pin_1, S3.Pin_2
  N4: Arduino1.D9, R6.Pin_0, S2.Pin_1, S2.Pin_2
  N5: Arduino1.D8, R5.Pin_0, S1.Pin_1, S1.Pin_2
  N6: Arduino1.D7, LED4.anode
  N7: Arduino1.D6, LED3.anode
  N8: Arduino1.D5, LED2.anode
  N9: Arduino1.D4, LED1.anode
  N10: Arduino1.+5V, R1.Pin_0, R2.Pin_0, R3.Pin_0, R4.Pin_0, R5.Pin_1, R6.Pin_1, R7.Pin_1, R8.Pin_1, J1.pin1
  N11: Arduino1.GND, S1.Pin_3, S1.Pin_4, S2.Pin_3, S2.Pin_4, S3.Pin_3, S3.Pin_4, S4.Pin_3, S4.Pin_4
  N12: R1.Pin_1, LED1.cathode
  N13: R2.Pin_1, LED2.cathode
  N14: R3.Pin_1, LED3.cathode
  N15: R4.Pin_1, LED4.cathode
